// Logisim project CPLD.circ as structural Verilog: 10 circuits, main circuit main
module main (
  input  CLK,
  input  MSG,
  output a1,
  output a2,
  output b1,
  output b2,
  output c1,
  output c2,
  output d1,
  output d2,
  output e1,
  output e2,
  output f1,
  output f2,
  output g1,
  output g2
);

  wire and_1_out, and_2_out, and_3_out, and_4_out, bcd_to_7segment_1_a, bcd_to_7segment_1_b,
       bcd_to_7segment_1_c, bcd_to_7segment_1_d, bcd_to_7segment_1_e, bcd_to_7segment_1_f,
       bcd_to_7segment_1_g, bcd_to_7segment_2_a, bcd_to_7segment_2_b, bcd_to_7segment_2_c,
       bcd_to_7segment_2_d, bcd_to_7segment_2_e, bcd_to_7segment_2_f, bcd_to_7segment_2_g, bit_counter_1_d0,
       bit_counter_1_d1, bit_counter_1_d2, bit_counter_1_d3, clock_divider_1_clk1, clock_divider_1_clk2,
       D0_1, D0_2, D1_1, D1_2, D2_1, D2_2, D3_1, D3_2, D_OUT, EN, or_1_out, shift_register_1_d0,
       shift_register_1_d1, shift_register_1_d2, shift_register_1_d3, shift_register_1_d4,
       shift_register_1_d5, shift_register_1_d6, shift_register_1_d7, state_machine_1_q_startbit;

  and and_1 (and_1_out, or_1_out, clock_divider_1_clk1);
  or or_1 (or_1_out, EN, ~state_machine_1_q_startbit);  // OR_Gate
  state_machine state_machine_1 (.Message(MSG), .CLK(and_1_out), .q_startbit(state_machine_1_q_startbit));
  clock_divider clock_divider_1 (.CLK(CLK), .CLK1(clock_divider_1_clk1), .CLK2(clock_divider_1_clk2));
  bcd_to_7segment bcd_to_7segment_1 (
    .D3(D3_2), .D2(D2_2), .D1(D1_2), .D0(D0_2), .a(bcd_to_7segment_1_a), .b(bcd_to_7segment_1_b),
    .c(bcd_to_7segment_1_c), .d(bcd_to_7segment_1_d), .e(bcd_to_7segment_1_e), .f(bcd_to_7segment_1_f),
    .g(bcd_to_7segment_1_g));
  not not_1 (a1, bcd_to_7segment_1_a);
  not not_2 (b1, bcd_to_7segment_1_b);
  not not_3 (c1, bcd_to_7segment_1_c);
  not not_4 (d1, bcd_to_7segment_1_d);
  not not_5 (e1, bcd_to_7segment_1_e);
  not not_6 (f1, bcd_to_7segment_1_f);
  not not_7 (g1, bcd_to_7segment_1_g);
  or or_2 (EN, and_4_out, and_2_out);
  and and_2 (and_2_out, and_3_out, ~D_OUT);  // AND_Gate
  and and_3 (and_3_out, bit_counter_1_d0, ~bit_counter_1_d1, ~bit_counter_1_d2, bit_counter_1_d3);  // AND_Gate
  bit_counter bit_counter_1 (
    .CLK(clock_divider_1_clk2), .CLR(and_1_out), .D0(bit_counter_1_d0), .D1(bit_counter_1_d1),
    .D2(bit_counter_1_d2), .D3(bit_counter_1_d3));
  shift_register shift_register_1 (
    .Message(MSG), .CLK(clock_divider_1_clk2), .D7(shift_register_1_d7), .D6(shift_register_1_d6),
    .D5(shift_register_1_d5), .D4(shift_register_1_d4), .D3(shift_register_1_d3), .D2(shift_register_1_d2),
    .D1(shift_register_1_d1), .D0(shift_register_1_d0), .D_OUT(D_OUT));
  and and_4 (and_4_out, ~bit_counter_1_d0, bit_counter_1_d1, ~bit_counter_1_d2, bit_counter_1_d3);  // AND_Gate
  bcd_to_7segment bcd_to_7segment_2 (
    .D3(D3_1), .D2(D2_1), .D1(D1_1), .D0(D0_1), .a(bcd_to_7segment_2_a), .b(bcd_to_7segment_2_b),
    .c(bcd_to_7segment_2_c), .d(bcd_to_7segment_2_d), .e(bcd_to_7segment_2_e), .f(bcd_to_7segment_2_f),
    .g(bcd_to_7segment_2_g));
  read_write_memory read_write_memory_1 (
    .D7_IN(shift_register_1_d7), .D6_IN(shift_register_1_d6), .D5_IN(shift_register_1_d5),
    .D4_IN(shift_register_1_d4), .D3_IN(shift_register_1_d3), .D2_IN(shift_register_1_d2),
    .D1_IN(shift_register_1_d1), .D0_IN(shift_register_1_d0), .EN(EN), .D7_OUT(D3_2), .D6_OUT(D2_2),
    .D5_OUT(D1_2), .D4_OUT(D0_2), .D3_OUT(D3_1), .D2_OUT(D2_1), .D1_OUT(D1_1), .D0_OUT(D0_1));
  not not_8 (a2, bcd_to_7segment_2_a);
  not not_9 (b2, bcd_to_7segment_2_b);
  not not_10 (c2, bcd_to_7segment_2_c);
  not not_11 (d2, bcd_to_7segment_2_d);
  not not_12 (e2, bcd_to_7segment_2_e);
  not not_13 (f2, bcd_to_7segment_2_f);
  not not_14 (g2, bcd_to_7segment_2_g);
endmodule

module state_machine (
  input  Message,
  input  CLK,
  output q_startbit
);

  wire and_1_out, and_2_out, and_3_out, and_4_out, d_ff_1_qn, d_ff_2_q, d_ff_3_q, d_ff_3_qn, not_1_out,
       or_1_out, xor_1_out;

  not not_1 (not_1_out, Message);
  and and_1 (and_1_out, or_1_out, not_1_out);
  or or_1 (or_1_out, and_2_out, q_startbit);
  D_Flip_Flop d_ff_1 (.D(and_1_out), .clk(CLK), .Q(q_startbit), .Qn(d_ff_1_qn));  // open: preset, reset
  xor xor_1 (xor_1_out, d_ff_3_q, d_ff_2_q);
  and and_2 (and_2_out, d_ff_3_q, d_ff_2_q);
  D_Flip_Flop d_ff_2 (.D(and_3_out), .clk(CLK), .Q(d_ff_2_q));  // open: Qn, preset, reset
  and and_3 (and_3_out, xor_1_out, not_1_out);
  D_Flip_Flop d_ff_3 (.D(and_4_out), .clk(CLK), .Q(d_ff_3_q), .Qn(d_ff_3_qn));  // open: preset, reset
  and and_4 (and_4_out, d_ff_3_qn, d_ff_1_qn, not_1_out);
endmodule

module bit_counter (
  input  CLK,
  input  CLR,
  output D0,
  output D1,
  output D2,
  output D3
);

  wire and_1_out, and_2_out, and_3_out, and_4_out, and_5_out, and_6_out, and_7_out, or_1_out, or_2_out, Q0n,
       Q1n, Q2n, Q3n, xor_1_out;

  D_Flip_Flop #(.trigger("falling")) d_ff_1 (.D(Q0n), .clk(CLK), .Q(D0), .Qn(Q0n), .reset(CLR));  // open: preset
  xor xor_1 (xor_1_out, Q0n, Q1n);
  D_Flip_Flop #(.trigger("falling")) d_ff_2 (.D(xor_1_out), .clk(CLK), .Q(D1), .Qn(Q1n), .reset(CLR));  // open: preset
  and and_1 (and_1_out, D0, D1, Q2n);
  and and_2 (and_2_out, Q1n, D2);
  and and_3 (and_3_out, Q0n, D2);
  or or_1 (or_1_out, and_1_out, and_2_out, and_3_out);
  D_Flip_Flop #(.trigger("falling")) d_ff_3 (.D(or_1_out), .clk(CLK), .Q(D2), .Qn(Q2n));  // open: preset, reset
  and and_4 (and_4_out, D3, Q0n);
  D_Flip_Flop #(.trigger("falling")) d_ff_4 (.D(or_2_out), .clk(CLK), .Q(D3), .Qn(Q3n), .reset(CLR));  // open: preset
  and and_5 (and_5_out, D3, Q1n);
  and and_6 (and_6_out, D3, Q2n);
  or or_2 (or_2_out, and_4_out, and_5_out, and_6_out, and_7_out);
  and and_7 (and_7_out, D0, D1, D2, Q3n);

  // Other names for the same wires on the sheet: Q0 = D0; Q1 = D1; Q2 = D2; Q3 = D3
endmodule

module shift_register (
  input  Message,
  input  CLK,
  output D7,
  output D6,
  output D5,
  output D4,
  output D3,
  output D2,
  output D1,
  output D0,
  output D_OUT
);

  D_Flip_Flop d_ff_1 (.D(Message), .clk(CLK), .Q(D7));  // open: Qn, preset, reset
  D_Flip_Flop d_ff_2 (.D(D7), .clk(CLK), .Q(D6));  // open: Qn, preset, reset
  D_Flip_Flop d_ff_3 (.D(D6), .clk(CLK), .Q(D5));  // open: Qn, preset, reset
  D_Flip_Flop d_ff_4 (.D(D5), .clk(CLK), .Q(D4));  // open: Qn, preset, reset
  D_Flip_Flop d_ff_5 (.D(D4), .clk(CLK), .Q(D3));  // open: Qn, preset, reset
  D_Flip_Flop d_ff_6 (.D(D3), .clk(CLK), .Q(D2));  // open: Qn, preset, reset
  D_Flip_Flop d_ff_7 (.D(D2), .clk(CLK), .Q(D1));  // open: Qn, preset, reset
  D_Flip_Flop d_ff_8 (.D(D1), .clk(CLK), .Q(D0));  // open: Qn, preset, reset
  D_Flip_Flop d_ff_9 (.D(D0), .clk(CLK), .Q(D_OUT));  // open: Qn, preset, reset
endmodule

module clock_divider (
  input  CLK,
  output CLK1,
  output CLK2
);

  wire d_ff_1_q, d_ff_1_qn, d_ff_2_qn, d_ff_3_q, d_ff_3_qn, d_ff_4_q, d_ff_4_qn, d_ff_5_qn;

  D_Flip_Flop d_ff_1 (.D(d_ff_1_qn), .clk(CLK), .Q(d_ff_1_q), .Qn(d_ff_1_qn));  // open: preset, reset
  D_Flip_Flop d_ff_2 (.D(d_ff_2_qn), .clk(d_ff_1_qn), .Q(CLK1), .Qn(d_ff_2_qn));  // open: preset, reset
  D_Flip_Flop d_ff_3 (.D(d_ff_3_qn), .clk(d_ff_2_qn), .Q(d_ff_3_q), .Qn(d_ff_3_qn));  // open: preset, reset
  D_Flip_Flop d_ff_4 (.D(d_ff_4_qn), .clk(d_ff_3_qn), .Q(d_ff_4_q), .Qn(d_ff_4_qn));  // open: preset, reset
  D_Flip_Flop d_ff_5 (.D(d_ff_5_qn), .clk(d_ff_4_qn), .Q(CLK2), .Qn(d_ff_5_qn));  // open: preset, reset
endmodule

module bcd_to_7segment (
  input  D3,
  input  D2,
  input  D1,
  input  D0,
  output a,
  output b,
  output c,
  output d,
  output e,
  output f,
  output g
);

  wire An, and_1_out, and_2_out, and_3_out, and_4_out, and_5_out, and_6_out, and_7_out, and_8_out, and_9_out,
       and_10_out, and_11_out, and_12_out, and_13_out, and_14_out, and_15_out, and_16_out, Bn, Cn, Dn;

  not not_1 (An, D3);
  not not_2 (Bn, D2);
  not not_3 (Cn, D1);
  not not_4 (Dn, D0);
  and and_1 (and_1_out, D2, D0);
  and and_2 (and_2_out, Bn, Dn);
  and and_3 (and_3_out, Bn, Dn);
  and and_4 (and_4_out, D1, Dn);
  or or_1 (a, and_2_out, D1, D3, and_1_out);
  or or_2 (c, Cn, D0, D2);
  or or_3 (e, and_3_out, and_4_out);
  and and_5 (and_5_out, Bn, D1);
  and and_6 (and_6_out, D2, Cn);
  and and_7 (and_7_out, D2, Dn);
  and and_8 (and_8_out, Bn, D1);
  or or_4 (g, and_5_out, and_6_out, and_7_out, D3);
  and and_9 (and_9_out, Cn, Dn);
  and and_10 (and_10_out, D1, D0);
  and and_11 (and_11_out, Bn, Dn);
  and and_12 (and_12_out, D2, Cn, D0);
  and and_13 (and_13_out, D1, Dn);
  and and_14 (and_14_out, Cn, Dn);
  and and_15 (and_15_out, Cn, D2);
  and and_16 (and_16_out, Dn, D2);
  or or_5 (b, and_9_out, Bn, and_10_out);
  or or_6 (d, and_11_out, and_8_out, and_12_out, and_13_out, D3);
  or or_7 (f, and_14_out, and_15_out, and_16_out, D3);

  // Other names for the same wires on the sheet: A_t = D3; B_t = D2; C_t = D1; D_t = D0
endmodule

module read_write_memory (
  input  D7_IN,
  input  D6_IN,
  input  D5_IN,
  input  D4_IN,
  input  D3_IN,
  input  D2_IN,
  input  D1_IN,
  input  D0_IN,
  input  EN,
  output D7_OUT,
  output D6_OUT,
  output D5_OUT,
  output D4_OUT,
  output D3_OUT,
  output D2_OUT,
  output D1_OUT,
  output D0_OUT
);

  wire d_ff_1_qn, d_ff_2_qn, d_ff_3_qn, d_ff_4_qn, d_ff_5_qn, d_ff_6_qn, d_ff_7_qn, d_ff_8_qn;

  D_Flip_Flop #(.trigger("falling")) d_ff_1 (.D(D7_IN), .clk(EN), .Q(D7_OUT), .Qn(d_ff_1_qn));  // open: preset, reset
  D_Flip_Flop #(.trigger("falling")) d_ff_2 (.D(D6_IN), .clk(EN), .Q(D6_OUT), .Qn(d_ff_2_qn));  // open: preset, reset
  D_Flip_Flop #(.trigger("falling")) d_ff_3 (.D(D5_IN), .clk(EN), .Q(D5_OUT), .Qn(d_ff_3_qn));  // open: preset, reset
  D_Flip_Flop #(.trigger("falling")) d_ff_4 (.D(D4_IN), .clk(EN), .Q(D4_OUT), .Qn(d_ff_4_qn));  // open: preset, reset
  D_Flip_Flop #(.trigger("falling")) d_ff_5 (.D(D3_IN), .clk(EN), .Q(D3_OUT), .Qn(d_ff_5_qn));  // open: preset, reset
  D_Flip_Flop #(.trigger("falling")) d_ff_6 (.D(D2_IN), .clk(EN), .Q(D2_OUT), .Qn(d_ff_6_qn));  // open: preset, reset
  D_Flip_Flop #(.trigger("falling")) d_ff_7 (.D(D1_IN), .clk(EN), .Q(D1_OUT), .Qn(d_ff_7_qn));  // open: preset, reset
  D_Flip_Flop #(.trigger("falling")) d_ff_8 (.D(D0_IN), .clk(EN), .Q(D0_OUT), .Qn(d_ff_8_qn));  // open: preset, reset
  // NoConnect on d_ff_1_qn
  // NoConnect on d_ff_2_qn
  // NoConnect on d_ff_3_qn
  // NoConnect on d_ff_4_qn
  // NoConnect on d_ff_5_qn
  // NoConnect on d_ff_6_qn
  // NoConnect on d_ff_7_qn
  // NoConnect on d_ff_8_qn
endmodule

module message (
  input  AUTO_RST,
  input  RST,
  input  CLK,
  output MSG
);

  wire and_1_out, and_2_out, counter_1_carry, not_1_out, or_1_out;
  wire [3:0] counter_1_q;

  not not_1 (not_1_out, RST);
  and and_1 (and_1_out, counter_1_carry, RST, not_1_out);
  or or_1 (or_1_out, and_1_out, and_2_out);
  and and_2 (and_2_out, AUTO_RST, counter_1_carry);
  Counter #(.max('ha), .ongoal("stay"), .width(4)) counter_1 (
    .clr(or_1_out), .clk(CLK), .carry(counter_1_carry), .Q(counter_1_q));  // open: load, up, count, D
  ROM #(.addrWidth(4), .dataWidth(1)) rom_1 (.addr(counter_1_q));  // open: data

  // Notes on the sheet:
  //   contents of rom_1 (hex, n*v repeats v):
  //   4*0 1 0 0 0 8*1
endmodule

module coc_divider (
  input  CLK,
  output CLK2
);

  wire d_ff_1_q, d_ff_1_qn, d_ff_2_q, d_ff_2_qn, d_ff_3_qn;

  D_Flip_Flop d_ff_1 (.D(d_ff_1_qn), .clk(CLK), .Q(d_ff_1_q), .Qn(d_ff_1_qn));  // open: preset, reset
  D_Flip_Flop d_ff_2 (.D(d_ff_2_qn), .clk(d_ff_1_qn), .Q(d_ff_2_q), .Qn(d_ff_2_qn));  // open: preset, reset
  D_Flip_Flop d_ff_3 (.D(d_ff_3_qn), .clk(d_ff_2_qn), .Q(CLK2), .Qn(d_ff_3_qn));  // open: preset, reset
endmodule

module main_test (
  input  AUTO_RST,
  input  RST
);

  wire and_1_out, and_2_out, and_3_out, and_4_out, bcd_to_7segment_1_a, bcd_to_7segment_1_b,
       bcd_to_7segment_1_c, bcd_to_7segment_1_d, bcd_to_7segment_1_e, bcd_to_7segment_1_f,
       bcd_to_7segment_1_g, bcd_to_7segment_2_a, bcd_to_7segment_2_b, bcd_to_7segment_2_c,
       bcd_to_7segment_2_d, bcd_to_7segment_2_e, bcd_to_7segment_2_f, bcd_to_7segment_2_g, CLK, CLK1, CLK2,
       counter_1_carry, counter_2_carry, counter_3_carry, D0_1, D0_2, D1_1, D1_2, D2_1, D2_2, D3_1, D3_2,
       D_OUT, EN, Msg, not_1_out, not_2_out, not_3_out, not_4_out, not_5_out, not_6_out, not_7_out,
       not_8_out, not_9_out, not_10_out, not_11_out, not_12_out, not_13_out, not_14_out, or_1_out,
       shift_register_1_d0, shift_register_1_d1, shift_register_1_d2, shift_register_1_d3,
       shift_register_1_d4, shift_register_1_d5, shift_register_1_d6, shift_register_1_d7,
       state_machine_1_q_startbit;
  wire [3:0] bit_counter_1_d0;

  Counter #(.max('h9), .ongoal("stay"), .trigger("falling"), .width(4)) counter_1 (
    .carry(counter_1_carry), .clk(CLK2));  // open: load, D, count, Q, up, clr
  // Probe on or_1_out
  Counter #(.max('h2), .ongoal("stay"), .trigger("falling"), .width(3)) counter_2 (
    .count(counter_1_carry), .carry(counter_2_carry), .clk(CLK1));  // open: load, D, Q, up, clr
  Counter #(.max('h2), .ongoal("stay"), .trigger("falling"), .width(2)) counter_3 (
    .count(counter_2_carry), .carry(counter_3_carry), .clk(CLK));  // open: load, D, Q, up, clr
  and and_1 (and_1_out, or_1_out, CLK1);
  Clock u_CLK (.out(CLK));
  or or_1 (or_1_out, EN, ~state_machine_1_q_startbit);  // OR_Gate
  state_machine state_machine_1 (.Message(Msg), .CLK(and_1_out), .q_startbit(state_machine_1_q_startbit));
  clock_divider clock_divider_1 (.CLK(CLK), .CLK1(CLK1), .CLK2(CLK2));
  message message_1 (.AUTO_RST(counter_3_carry), .RST(RST), .CLK(CLK2), .MSG(Msg));
  bcd_to_7segment bcd_to_7segment_1 (
    .D3(D3_2), .D2(D2_2), .D1(D1_2), .D0(D0_2), .a(bcd_to_7segment_1_a), .b(bcd_to_7segment_1_b),
    .c(bcd_to_7segment_1_c), .d(bcd_to_7segment_1_d), .e(bcd_to_7segment_1_e), .f(bcd_to_7segment_1_f),
    .g(bcd_to_7segment_1_g));
  not not_1 (not_1_out, bcd_to_7segment_1_a);
  not not_2 (not_2_out, bcd_to_7segment_1_b);
  not not_3 (not_3_out, bcd_to_7segment_1_c);
  not not_4 (not_4_out, bcd_to_7segment_1_d);
  not not_5 (not_5_out, bcd_to_7segment_1_e);
  not not_6 (not_6_out, bcd_to_7segment_1_f);
  not not_7 (not_7_out, bcd_to_7segment_1_g);
  // Probe on EN
  _7_Segment_Display #(.active("false"), .decimalPoint("false")) u_7_segment_display_1 (
    .g(not_7_out), .f(not_6_out), .a(not_1_out), .b(not_2_out), .e(not_5_out), .d(not_4_out), .c(not_3_out));
  or or_2 (EN, and_4_out, and_2_out);
  and and_2 (and_2_out, and_3_out, ~D_OUT);  // AND_Gate
  and and_3 (and_3_out, bit_counter_1_d0[0], ~bit_counter_1_d0[1], ~bit_counter_1_d0[2], bit_counter_1_d0[3]);  // AND_Gate
  bit_counter bit_counter_1 (
    .CLK(CLK2), .CLR(and_1_out), .D0(bit_counter_1_d0[0]), .D1(bit_counter_1_d0[1]),
    .D2(bit_counter_1_d0[2]), .D3(bit_counter_1_d0[3]));
  shift_register shift_register_1 (
    .Message(Msg), .CLK(CLK2), .D7(shift_register_1_d7), .D6(shift_register_1_d6), .D5(shift_register_1_d5),
    .D4(shift_register_1_d4), .D3(shift_register_1_d3), .D2(shift_register_1_d2), .D1(shift_register_1_d1),
    .D0(shift_register_1_d0), .D_OUT(D_OUT));
  and and_4 (and_4_out, ~bit_counter_1_d0[0], bit_counter_1_d0[1], ~bit_counter_1_d0[2], bit_counter_1_d0[3]);  // AND_Gate
  read_write_memory read_write_memory_1 (
    .D7_IN(shift_register_1_d7), .D6_IN(shift_register_1_d6), .D5_IN(shift_register_1_d5),
    .D4_IN(shift_register_1_d4), .D3_IN(shift_register_1_d3), .D2_IN(shift_register_1_d2),
    .D1_IN(shift_register_1_d1), .D0_IN(shift_register_1_d0), .EN(EN), .D7_OUT(D3_2), .D6_OUT(D2_2),
    .D5_OUT(D1_2), .D4_OUT(D0_2), .D3_OUT(D3_1), .D2_OUT(D2_1), .D1_OUT(D1_1), .D0_OUT(D0_1));
  bcd_to_7segment bcd_to_7segment_2 (
    .D3(D3_1), .D2(D2_1), .D1(D1_1), .D0(D0_1), .a(bcd_to_7segment_2_a), .b(bcd_to_7segment_2_b),
    .c(bcd_to_7segment_2_c), .d(bcd_to_7segment_2_d), .e(bcd_to_7segment_2_e), .f(bcd_to_7segment_2_f),
    .g(bcd_to_7segment_2_g));
  // Probe on bit_counter_1_d0
  not not_8 (not_8_out, bcd_to_7segment_2_a);
  not not_9 (not_9_out, bcd_to_7segment_2_b);
  not not_10 (not_10_out, bcd_to_7segment_2_c);
  not not_11 (not_11_out, bcd_to_7segment_2_d);
  not not_12 (not_12_out, bcd_to_7segment_2_e);
  not not_13 (not_13_out, bcd_to_7segment_2_f);
  not not_14 (not_14_out, bcd_to_7segment_2_g);
  _7_Segment_Display #(.active("false"), .decimalPoint("false")) u_7_segment_display_2 (
    .g(not_14_out), .f(not_13_out), .a(not_8_out), .b(not_9_out), .e(not_12_out), .d(not_11_out),
    .c(not_10_out));
endmodule
